// Logisim project 16bit_16bit_AND.circ as structural Verilog: 1 circuit, main circuit and16_16
module and16_16 (
  input  [15:0] InB,
  input  [15:0] InA,
  output [15:0] Out_Pins
);

  _7408 #(.ShowInternalStructure("true")) u_7408_1 (
    .pin1(InA[15]), .pin2(InB[15]), .pin3(Out_Pins[15]), .pin4(InA[14]), .pin5(InB[14]), .pin6(Out_Pins[14]),
    .pin13(InA[12]), .pin12(InB[12]), .pin11(Out_Pins[12]), .pin10(InA[13]), .pin9(InB[13]),
    .pin8(Out_Pins[13]));
  _7408 #(.ShowInternalStructure("true")) u_7408_2 (
    .pin1(InA[11]), .pin2(InA[9]), .pin3(Out_Pins[11]), .pin4(InA[10]), .pin5(InA[8]), .pin6(Out_Pins[10]),
    .pin13(InB[10]), .pin12(InB[8]), .pin11(Out_Pins[8]), .pin10(InB[11]), .pin9(InB[9]), .pin8(Out_Pins[9]));
  _7408 #(.ShowInternalStructure("true")) u_7408_3 (
    .pin1(InA[7]), .pin2(InB[7]), .pin3(Out_Pins[7]), .pin4(InA[6]), .pin5(InB[6]), .pin6(Out_Pins[6]),
    .pin13(InA[4]), .pin12(InB[4]), .pin11(Out_Pins[4]), .pin10(InA[5]), .pin9(InB[5]), .pin8(Out_Pins[5]));
  _7408 #(.ShowInternalStructure("true")) u_7408_4 (
    .pin1(InA[3]), .pin2(InB[3]), .pin3(Out_Pins[3]), .pin4(InA[2]), .pin5(InB[2]), .pin6(Out_Pins[2]),
    .pin13(InA[0]), .pin12(InB[0]), .pin11(Out_Pins[0]), .pin10(InA[1]), .pin9(InB[1]), .pin8(Out_Pins[1]));
endmodule
