// Logisim project 16bit_Buffer_Tristate.circ as structural Verilog: 1 circuit, main circuit Buffer_16bit_Tristate
module Buffer_16bit_Tristate (
  input  OE,
  input  [15:0] Data_in,
  output [15:0] Data_out
);

  _74244 #(.ShowInternalStructure("true")) u_74244_1 (
    .pin1(OE), .pin2(Data_in[0]), .pin3(Data_out[4]), .pin4(Data_in[1]), .pin5(Data_out[5]),
    .pin6(Data_in[2]), .pin7(Data_out[6]), .pin8(Data_in[3]), .pin9(Data_out[7]), .pin19(OE),
    .pin18(Data_out[0]), .pin17(Data_in[4]), .pin16(Data_out[1]), .pin15(Data_in[5]), .pin14(Data_out[2]),
    .pin13(Data_in[6]), .pin12(Data_out[3]), .pin11(Data_in[7]));
  _74244 #(.ShowInternalStructure("true")) u_74244_2 (
    .pin1(OE), .pin2(Data_in[8]), .pin3(Data_out[12]), .pin4(Data_in[9]), .pin5(Data_out[13]),
    .pin6(Data_in[10]), .pin7(Data_out[14]), .pin8(Data_in[11]), .pin9(Data_out[15]), .pin19(OE),
    .pin18(Data_out[8]), .pin17(Data_in[12]), .pin16(Data_out[9]), .pin15(Data_in[13]), .pin14(Data_out[10]),
    .pin13(Data_in[14]), .pin12(Data_out[11]), .pin11(Data_in[15]));
endmodule
