// Logisim project 16bit_FullAdder.circ as structural Verilog: 1 circuit, main circuit fulladder_16
// Adder 16
module fulladder_16 (
  input  [15:0] B_in,
  input  [15:0] A_in,
  output [15:0] AddOut,
  output OverFlow
);

  wire n74283_1_pin7, n74283_2_pin7, n74283_3_pin7;

  _74283 #(.ShowInternalStructure("true")) u_74283_1 (
    .pin1(AddOut[13]), .pin2(B_in[13]), .pin3(A_in[13]), .pin4(AddOut[12]), .pin5(A_in[12]), .pin6(B_in[12]),
    .pin7(n74283_1_pin7), .pin15(B_in[14]), .pin14(A_in[14]), .pin13(AddOut[14]), .pin12(A_in[15]),
    .pin11(B_in[15]), .pin10(AddOut[15]), .pin9(OverFlow));
  _74283 #(.ShowInternalStructure("true")) u_74283_2 (
    .pin1(AddOut[9]), .pin2(B_in[9]), .pin3(A_in[9]), .pin4(AddOut[8]), .pin5(A_in[8]), .pin6(B_in[8]),
    .pin7(n74283_2_pin7), .pin15(B_in[10]), .pin14(A_in[10]), .pin13(AddOut[10]), .pin12(A_in[11]),
    .pin11(B_in[11]), .pin10(AddOut[11]), .pin9(n74283_1_pin7));
  _74283 #(.ShowInternalStructure("true")) u_74283_3 (
    .pin1(AddOut[5]), .pin2(B_in[5]), .pin3(A_in[5]), .pin4(AddOut[4]), .pin5(A_in[4]), .pin6(B_in[4]),
    .pin7(n74283_3_pin7), .pin15(B_in[6]), .pin14(A_in[6]), .pin13(AddOut[6]), .pin12(A_in[7]),
    .pin11(B_in[7]), .pin10(AddOut[7]), .pin9(n74283_2_pin7));
  _74283 #(.ShowInternalStructure("true")) u_74283_4 (
    .pin1(AddOut[1]), .pin2(B_in[1]), .pin3(A_in[1]), .pin4(AddOut[0]), .pin5(A_in[0]), .pin6(B_in[0]),
    .pin15(B_in[2]), .pin14(A_in[2]), .pin13(AddOut[2]), .pin12(A_in[3]), .pin11(B_in[3]), .pin10(AddOut[3]),
    .pin9(n74283_3_pin7));  // open: pin7
endmodule
