// Logisim project 16bit_FullAdderTest.circ as structural Verilog: 1 circuit, main circuit main
module main (
  output [15:0] out_1,
  output [15:0] out_2,
  output out_3
);

  fulladder_16 fulladder_16_1 (.B_in(16'hfffa), .A_in(16'h6), .AddOut(out_1), .OverFlow(out_3));

  assign out_2 = out_1;
endmodule
