// Logisim project 16bit_Multiplex_NOT.circ as structural Verilog: 1 circuit, main circuit Multiplex16_XOR
module Multiplex16_XOR (
  input  Invert,
  input  [15:0] IN_Pins,
  output [15:0] OUT_Pins
);

  _7486 #(.ShowInternalStructure("true")) u_7486_1 (
    .pin1(Invert), .pin2(IN_Pins[13]), .pin3(OUT_Pins[13]), .pin4(Invert), .pin5(IN_Pins[12]),
    .pin6(OUT_Pins[12]), .pin13(Invert), .pin12(IN_Pins[14]), .pin11(OUT_Pins[14]), .pin10(Invert),
    .pin9(IN_Pins[15]), .pin8(OUT_Pins[15]));
  _7486 #(.ShowInternalStructure("true")) u_7486_2 (
    .pin1(Invert), .pin2(IN_Pins[9]), .pin3(OUT_Pins[9]), .pin4(Invert), .pin5(IN_Pins[8]),
    .pin6(OUT_Pins[8]), .pin13(Invert), .pin12(IN_Pins[10]), .pin11(OUT_Pins[10]), .pin10(Invert),
    .pin9(IN_Pins[11]), .pin8(OUT_Pins[11]));
  _7486 #(.ShowInternalStructure("true")) u_7486_3 (
    .pin1(Invert), .pin2(IN_Pins[5]), .pin3(OUT_Pins[5]), .pin4(Invert), .pin5(IN_Pins[4]),
    .pin6(OUT_Pins[4]), .pin13(Invert), .pin12(IN_Pins[6]), .pin11(OUT_Pins[6]), .pin10(Invert),
    .pin9(IN_Pins[7]), .pin8(OUT_Pins[7]));
  _7486 #(.ShowInternalStructure("true")) u_7486_4 (
    .pin1(Invert), .pin2(IN_Pins[1]), .pin3(OUT_Pins[1]), .pin4(Invert), .pin5(IN_Pins[0]),
    .pin6(OUT_Pins[0]), .pin13(Invert), .pin12(IN_Pins[2]), .pin11(OUT_Pins[2]), .pin10(Invert),
    .pin9(IN_Pins[3]), .pin8(OUT_Pins[3]));
endmodule
