// Logisim project 16bit_MultiplexerTest.circ as structural Verilog: 1 circuit, main circuit main
module main (
  input  [15:0] in_1,
  input  [15:0] in_2,
  output [15:0] out_3
);

  wire dipswitch_1_sw1;

  DipSwitch #(.number(2)) dipswitch_1 (.sw1(dipswitch_1_sw1));  // open: sw2
  // multiplex16 multiplex16_1: pin names not known; wires that end beside it: dipswitch_1_sw1, in_1, in_2, out_3

  // Notes on the sheet:
  //   in_1: initial=0x1111
endmodule
