// Logisim project 16bit_Multiplexer_standalone.circ as structural Verilog: 1 circuit, main circuit multiplex16_standalone
module multiplex16_standalone (
  input  Strobe,
  input  Sel,
  input  [15:0] InB,
  input  [15:0] InA,
  output [15:0] Out_Pins
);

  _74157 #(.ShowInternalStructure("true")) u_74157_1 (
    .pin1(Sel), .pin2(InA[15]), .pin3(InB[15]), .pin4(Out_Pins[15]), .pin5(InA[14]), .pin6(InB[14]),
    .pin7(Out_Pins[14]), .pin15(Strobe), .pin14(InA[12]), .pin13(InB[12]), .pin12(Out_Pins[12]),
    .pin11(InA[13]), .pin10(InB[13]), .pin9(Out_Pins[13]));
  _74157 #(.ShowInternalStructure("true")) u_74157_2 (
    .pin1(Sel), .pin2(InA[11]), .pin3(InB[11]), .pin4(Out_Pins[11]), .pin5(InA[10]), .pin6(InB[10]),
    .pin7(Out_Pins[10]), .pin15(Strobe), .pin14(InA[8]), .pin13(InB[8]), .pin12(Out_Pins[8]), .pin11(InA[9]),
    .pin10(InB[9]), .pin9(Out_Pins[9]));
  _74157 #(.ShowInternalStructure("true")) u_74157_3 (
    .pin1(Sel), .pin2(InA[7]), .pin3(InB[7]), .pin4(Out_Pins[7]), .pin5(InA[6]), .pin6(InB[6]),
    .pin7(Out_Pins[6]), .pin15(Strobe), .pin14(InA[4]), .pin13(InB[4]), .pin12(Out_Pins[4]), .pin11(InA[5]),
    .pin10(InB[5]), .pin9(Out_Pins[5]));
  _74157 #(.ShowInternalStructure("true")) u_74157_4 (
    .pin1(Sel), .pin2(InA[3]), .pin3(InB[3]), .pin4(Out_Pins[3]), .pin5(InA[2]), .pin6(InB[2]),
    .pin7(Out_Pins[2]), .pin15(Strobe), .pin14(InA[0]), .pin13(InB[0]), .pin12(Out_Pins[0]), .pin11(InA[1]),
    .pin10(InB[1]), .pin9(Out_Pins[1]));
endmodule
