// Logisim project 16bit_NOT.circ as structural Verilog: 1 circuit, main circuit not_16bit
module not_16bit (
  input  [15:0] In_16,
  output [15:0] Out_16
);

  inverter_8bit inverter_8bit_1 (.In_8(In_16[7:0]), .Out_8(Out_16[7:0]));
  inverter_8bit inverter_8bit_2 (.In_8(In_16[15:8]), .Out_8(Out_16[15:8]));

  // Notes on the sheet:
  //   In_16: initial=0x1100110
endmodule
