// Logisim project 16bit_register.circ as structural Verilog: 1 circuit, main circuit register_16bit
module register_16bit (
  input  Clock,
  input  Enable_low,
  input  [15:0] Data_In,
  output [15:0] Data_OUT
);

  _74377 #(.ShowInternalStructure("true")) u_74377_1 (
    .pin1(Enable_low), .pin2(Data_OUT[8]), .pin3(Data_In[8]), .pin4(Data_In[9]), .pin5(Data_OUT[9]),
    .pin6(Data_OUT[10]), .pin7(Data_In[10]), .pin8(Data_In[11]), .pin9(Data_OUT[11]), .pin19(Data_OUT[15]),
    .pin18(Data_In[15]), .pin17(Data_In[14]), .pin16(Data_OUT[14]), .pin15(Data_OUT[13]),
    .pin14(Data_In[13]), .pin13(Data_In[12]), .pin12(Data_OUT[12]), .pin11(Clock));
  _74377 #(.ShowInternalStructure("true")) u_74377_2 (
    .pin1(Enable_low), .pin2(Data_OUT[0]), .pin3(Data_In[0]), .pin4(Data_In[1]), .pin5(Data_OUT[1]),
    .pin6(Data_OUT[2]), .pin7(Data_In[2]), .pin8(Data_In[3]), .pin9(Data_OUT[3]), .pin19(Data_OUT[7]),
    .pin18(Data_In[7]), .pin17(Data_In[6]), .pin16(Data_OUT[6]), .pin15(Data_OUT[5]), .pin14(Data_In[5]),
    .pin13(Data_In[4]), .pin12(Data_OUT[4]), .pin11(Clock));
endmodule
