// Logisim project 16bit_register_tristate.circ as structural Verilog: 1 circuit, main circuit register_16bit_tristate
module register_16bit_tristate (
  input  Output_Disable2,
  input  Output_Disable1,
  input  CLR,
  input  ENABLE2,
  input  ENABLE1,
  input  Clock,
  input  [15:0] Data_IN,
  output [15:0] Data_OUT
);

  IC_74173 ic_74173_1 (
    .D1(Data_IN[0]), .D2(Data_IN[1]), .D3(Data_IN[2]), .D4(Data_IN[3]), .CLK(Clock), .CE1(ENABLE1),
    .CE2(ENABLE2), .CLR(CLR), .OE1(Output_Disable1), .OE2(Output_Disable2), .Q1(Data_OUT[0]),
    .Q2(Data_OUT[1]), .Q3(Data_OUT[2]), .Q4(Data_OUT[3]));
  IC_74173 ic_74173_2 (
    .D1(Data_IN[4]), .D2(Data_IN[5]), .D3(Data_IN[6]), .D4(Data_IN[7]), .CLK(Clock), .CE1(ENABLE1),
    .CE2(ENABLE2), .CLR(CLR), .OE1(Output_Disable1), .OE2(Output_Disable2), .Q1(Data_OUT[4]),
    .Q2(Data_OUT[5]), .Q3(Data_OUT[6]), .Q4(Data_OUT[7]));
  IC_74173 ic_74173_3 (
    .D1(Data_IN[8]), .D2(Data_IN[9]), .D3(Data_IN[10]), .D4(Data_IN[11]), .CLK(Clock), .CE1(ENABLE1),
    .CE2(ENABLE2), .CLR(CLR), .OE1(Output_Disable1), .OE2(Output_Disable2), .Q1(Data_OUT[8]),
    .Q2(Data_OUT[9]), .Q3(Data_OUT[10]), .Q4(Data_OUT[11]));
  IC_74173 ic_74173_4 (
    .D1(Data_IN[12]), .D2(Data_IN[13]), .D3(Data_IN[14]), .D4(Data_IN[15]), .CLK(Clock), .CE1(ENABLE1),
    .CE2(ENABLE2), .CLR(CLR), .OE1(Output_Disable1), .OE2(Output_Disable2), .Q1(Data_OUT[12]),
    .Q2(Data_OUT[13]), .Q3(Data_OUT[14]), .Q4(Data_OUT[15]));
endmodule
