// Logisim project 8bit_OR_74HC4078.circ as structural Verilog: 1 circuit, main circuit OR_8bit
module OR_8bit (
  input  [7:0] In_OR,
  output Out_NOR,
  output Out_OR
);

  or or_1 (Out_OR, In_OR[0], In_OR[1], In_OR[2], In_OR[3], In_OR[4], In_OR[5], In_OR[6], In_OR[7]);
  not not_1 (Out_NOR, Out_OR);
endmodule
