// Logisim project 8fach_Inverter_74HC540.circ as structural Verilog: 1 circuit, main circuit inverter_8bit
module inverter_8bit (
  input  [7:0] In_8,
  output [7:0] Out_8
);

  _7404 #(.ShowInternalStructure("true")) u_7404_1 (
    .pin3(In_8[7]), .pin4(Out_8[7]), .pin5(In_8[6]), .pin6(Out_8[6]));  // open: pin1, pin2, pin13, pin12, pin11, pin10, pin9, pin8
  _7404 #(.ShowInternalStructure("true")) u_7404_2 (
    .pin1(In_8[2]), .pin2(Out_8[2]), .pin3(In_8[1]), .pin4(Out_8[1]), .pin5(In_8[0]), .pin6(Out_8[0]),
    .pin13(In_8[3]), .pin12(Out_8[3]), .pin11(In_8[4]), .pin10(Out_8[4]), .pin9(In_8[5]), .pin8(Out_8[5]));
endmodule
