// Logisim project ALU_.circ as structural Verilog: 1 circuit, main circuit ALU
module ALU (
  input  no,
  input  f,
  input  nx,
  input  zx,
  input  [15:0] x,
  input  ny,
  input  zy,
  input  [15:0] y,
  output [15:0] ALU_out,
  output zr,
  output ng
);

  wire n7408_1_pin9, n7408_1_pin10;

  _7408 #(.ShowInternalStructure("true")) u_7408_1 (
    .pin10(n7408_1_pin10), .pin9(n7408_1_pin9), .pin8(zr));  // open: pin1, pin2, pin3, pin4, pin5, pin6, pin13, pin12, pin11

  assign ng = ALU_out[15];
endmodule
