// Logisim project CPU.circ as structural Verilog: 1 circuit, main circuit cpu
module cpu (
  input  [15:0] Instruction,
  input  Clock,
  input  [15:0] inM,
  input  Reset,
  output [15:0] OutM,
  output [15:0] Debug_D,
  output [15:0] Debug_A,
  output [14:0] AddressM,
  output [14:0] AddressInstr,
  output writeM
);

  wire n7404_1_pin2, n7404_1_pin5, n7404_1_pin6, n7404_1_pin10, n7408_1_pin1, n7408_1_pin3, n7408_1_pin6,
       n7408_1_pin11, n7408_1_pin13, n7408_2_pin3, n7432_1_pin1, n7432_1_pin2, n7432_1_pin3, n7432_1_pin10,
       n7432_1_pin12;

  _7408 #(.ShowInternalStructure("true")) u_7408_1 (
    .pin1(n7408_1_pin1), .pin2(Instruction[1]), .pin3(n7408_1_pin3), .pin4(Instruction[15]),
    .pin5(Instruction[4]), .pin6(n7408_1_pin6), .pin13(n7408_1_pin13), .pin12(Instruction[15]),
    .pin11(n7408_1_pin11), .pin10(Instruction[3]), .pin9(Instruction[15]), .pin8(writeM));
  _7404 #(.ShowInternalStructure("true")) u_7404_1 (
    .pin1(Reset), .pin2(n7404_1_pin2), .pin5(n7404_1_pin5), .pin6(n7404_1_pin6), .pin11(n7408_1_pin6),
    .pin10(n7404_1_pin10), .pin9(Instruction[5]), .pin8(n7408_1_pin13));  // open: pin3, pin4, pin13, pin12
  _7432 #(.ShowInternalStructure("true")) u_7432_1 (
    .pin1(n7432_1_pin1), .pin2(n7432_1_pin2), .pin3(n7432_1_pin3), .pin13(n7408_1_pin3),
    .pin12(n7432_1_pin12), .pin11(n7432_1_pin1), .pin10(n7432_1_pin10), .pin9(n7408_1_pin1),
    .pin8(n7404_1_pin5));  // open: pin4, pin5, pin6
  _7408 #(.ShowInternalStructure("true")) u_7408_2 (
    .pin1(n7432_1_pin3), .pin2(Instruction[15]), .pin3(n7408_2_pin3), .pin13(n7404_1_pin6),
    .pin12(Instruction[0]), .pin11(n7432_1_pin2), .pin10(Instruction[2]), .pin9(n7432_1_pin10),
    .pin8(n7432_1_pin12));  // open: pin4, pin5, pin6
endmodule
