// Logisim project Delay_128_inverter.circ as structural Verilog: 1 circuit, main circuit delay_128
module delay_128 (
  input  Data_IN,
  output Data_OUT
);

  wire delay_32_1_data_out, delay_32_2_data_out, delay_32_3_data_out;

  delay_32 delay_32_1 (.Data_IN(Data_IN), .Data_OUT(delay_32_1_data_out));
  delay_32 delay_32_2 (.Data_IN(delay_32_1_data_out), .Data_OUT(delay_32_2_data_out));
  delay_32 delay_32_3 (.Data_IN(delay_32_2_data_out), .Data_OUT(delay_32_3_data_out));
  delay_32 delay_32_4 (.Data_IN(delay_32_3_data_out), .Data_OUT(Data_OUT));
endmodule
