// Logisim project Delay_32_inverter.circ as structural Verilog: 1 circuit, main circuit delay_32
module delay_32 (
  input  Data_IN,
  output Data_OUT
);

  wire delay_1_data_out, delay_2_data_out, delay_3_data_out;

  delay delay_1 (.Data_IN(Data_IN), .Data_OUT(delay_1_data_out));
  delay delay_2 (.Data_IN(delay_1_data_out), .Data_OUT(delay_2_data_out));
  delay delay_3 (.Data_IN(delay_2_data_out), .Data_OUT(delay_3_data_out));
  delay delay_4 (.Data_IN(delay_3_data_out), .Data_OUT(Data_OUT));
endmodule
