// Logisim project Delay_8_inverter.circ as structural Verilog: 1 circuit, main circuit delay
module delay (
  input  Data_IN,
  output Data_OUT
);

  wire not_1_out, not_2_out, not_3_out, not_4_out, not_5_out, not_6_out, not_7_out;

  not not_1 (not_1_out, Data_IN);
  not not_2 (not_2_out, not_1_out);
  not not_3 (not_3_out, not_6_out);
  not not_4 (not_4_out, not_3_out);
  not not_5 (not_5_out, not_2_out);
  not not_6 (not_6_out, not_5_out);
  not not_7 (not_7_out, not_4_out);
  not not_8 (Data_OUT, not_7_out);
endmodule
