// Logisim project Program_Counter.circ as structural Verilog: 4 circuits, main circuit PC
module PC (
  input  [15:0] ADDR_IN,
  input  RESET,
  input  LOAD,
  input  INC,
  input  Clock,
  output [15:0] ADDR_OUT
);

  wire [15:0] fulladder_16_1_addout, multiplex16_1_out_pins, multiplex16_2_out_pins, multiplex16_3_out_pins;

  register_16bit register_16bit_1 (
    .Clock(Clock), .Enable_low(1'b0), .Data_In(multiplex16_3_out_pins), .Data_OUT(ADDR_OUT));
  fulladder_16 fulladder_16_1 (.B_in(ADDR_OUT), .A_in(16'h1), .AddOut(fulladder_16_1_addout));  // open: OverFlow
  multiplex16 multiplex16_1 (
    .Sel(INC), .InB(fulladder_16_1_addout), .InA(ADDR_OUT), .Out_Pins(multiplex16_1_out_pins));  // open: Strobe
  multiplex16 multiplex16_2 (
    .Sel(LOAD), .InB(ADDR_IN), .InA(multiplex16_1_out_pins), .Out_Pins(multiplex16_2_out_pins));  // open: Strobe
  multiplex16 multiplex16_3 (
    .Strobe(RESET), .InA(multiplex16_2_out_pins), .Out_Pins(multiplex16_3_out_pins));  // open: Sel, InB
endmodule

module register_16bit (
  input  Clock,
  input  Enable_low,
  input  [15:0] Data_In,
  output [15:0] Data_OUT
);

  _74377 #(.ShowInternalStructure("true")) u_74377_1 (
    .pin1(Enable_low), .pin2(Data_OUT[8]), .pin3(Data_In[8]), .pin4(Data_In[9]), .pin5(Data_OUT[9]),
    .pin6(Data_OUT[10]), .pin7(Data_In[10]), .pin8(Data_In[11]), .pin9(Data_OUT[11]), .pin19(Data_OUT[15]),
    .pin18(Data_In[15]), .pin17(Data_In[14]), .pin16(Data_OUT[14]), .pin15(Data_OUT[13]),
    .pin14(Data_In[13]), .pin13(Data_In[12]), .pin12(Data_OUT[12]), .pin11(Clock));
  _74377 #(.ShowInternalStructure("true")) u_74377_2 (
    .pin1(Enable_low), .pin2(Data_OUT[0]), .pin3(Data_In[0]), .pin4(Data_In[1]), .pin5(Data_OUT[1]),
    .pin6(Data_OUT[2]), .pin7(Data_In[2]), .pin8(Data_In[3]), .pin9(Data_OUT[3]), .pin19(Data_OUT[7]),
    .pin18(Data_In[7]), .pin17(Data_In[6]), .pin16(Data_OUT[6]), .pin15(Data_OUT[5]), .pin14(Data_In[5]),
    .pin13(Data_In[4]), .pin12(Data_OUT[4]), .pin11(Clock));
endmodule

// Adder 16
module fulladder_16 (
  input  [15:0] B_in,
  input  [15:0] A_in,
  output [15:0] AddOut,
  output OverFlow
);

  wire n74283_1_pin7, n74283_2_pin7, n74283_3_pin7;

  _74283 #(.ShowInternalStructure("true")) u_74283_1 (
    .pin1(AddOut[13]), .pin2(B_in[13]), .pin3(A_in[13]), .pin4(AddOut[12]), .pin5(A_in[12]), .pin6(B_in[12]),
    .pin7(n74283_1_pin7), .pin15(B_in[14]), .pin14(A_in[14]), .pin13(AddOut[14]), .pin12(A_in[15]),
    .pin11(B_in[15]), .pin10(AddOut[15]), .pin9(OverFlow));
  _74283 #(.ShowInternalStructure("true")) u_74283_2 (
    .pin1(AddOut[9]), .pin2(B_in[9]), .pin3(A_in[9]), .pin4(AddOut[8]), .pin5(A_in[8]), .pin6(B_in[8]),
    .pin7(n74283_2_pin7), .pin15(B_in[10]), .pin14(A_in[10]), .pin13(AddOut[10]), .pin12(A_in[11]),
    .pin11(B_in[11]), .pin10(AddOut[11]), .pin9(n74283_1_pin7));
  _74283 #(.ShowInternalStructure("true")) u_74283_3 (
    .pin1(AddOut[5]), .pin2(B_in[5]), .pin3(A_in[5]), .pin4(AddOut[4]), .pin5(A_in[4]), .pin6(B_in[4]),
    .pin7(n74283_3_pin7), .pin15(B_in[6]), .pin14(A_in[6]), .pin13(AddOut[6]), .pin12(A_in[7]),
    .pin11(B_in[7]), .pin10(AddOut[7]), .pin9(n74283_2_pin7));
  _74283 #(.ShowInternalStructure("true")) u_74283_4 (
    .pin1(AddOut[1]), .pin2(B_in[1]), .pin3(A_in[1]), .pin4(AddOut[0]), .pin5(A_in[0]), .pin6(B_in[0]),
    .pin15(B_in[2]), .pin14(A_in[2]), .pin13(AddOut[2]), .pin12(A_in[3]), .pin11(B_in[3]), .pin10(AddOut[3]),
    .pin9(n74283_3_pin7));  // open: pin7
endmodule

module multiplex16 (
  input  Strobe,
  input  Sel,
  input  [15:0] InB,
  input  [15:0] InA,
  output [15:0] Out_Pins
);

  _74157 #(.ShowInternalStructure("true")) u_74157_1 (
    .pin1(Sel), .pin2(InA[15]), .pin3(InB[15]), .pin4(Out_Pins[15]), .pin5(InA[14]), .pin6(InB[14]),
    .pin7(Out_Pins[14]), .pin15(Strobe), .pin14(InA[12]), .pin13(InB[12]), .pin12(Out_Pins[12]),
    .pin11(InA[13]), .pin10(InB[13]), .pin9(Out_Pins[13]));
  _74157 #(.ShowInternalStructure("true")) u_74157_2 (
    .pin1(Sel), .pin2(InA[11]), .pin3(InB[11]), .pin4(Out_Pins[11]), .pin5(InA[10]), .pin6(InB[10]),
    .pin7(Out_Pins[10]), .pin15(Strobe), .pin14(InA[8]), .pin13(InB[8]), .pin12(Out_Pins[8]), .pin11(InA[9]),
    .pin10(InB[9]), .pin9(Out_Pins[9]));
  _74157 #(.ShowInternalStructure("true")) u_74157_3 (
    .pin1(Sel), .pin2(InA[7]), .pin3(InB[7]), .pin4(Out_Pins[7]), .pin5(InA[6]), .pin6(InB[6]),
    .pin7(Out_Pins[6]), .pin15(Strobe), .pin14(InA[4]), .pin13(InB[4]), .pin12(Out_Pins[4]), .pin11(InA[5]),
    .pin10(InB[5]), .pin9(Out_Pins[5]));
  _74157 #(.ShowInternalStructure("true")) u_74157_4 (
    .pin1(Sel), .pin2(InA[3]), .pin3(InB[3]), .pin4(Out_Pins[3]), .pin5(InA[2]), .pin6(InB[2]),
    .pin7(Out_Pins[2]), .pin15(Strobe), .pin14(InA[0]), .pin13(InB[0]), .pin12(Out_Pins[0]), .pin11(InA[1]),
    .pin10(InB[1]), .pin9(Out_Pins[1]));
endmodule
