// Logisim project RAM_Test.circ as structural Verilog: 2 circuits, main circuit main
module main (
  input  [15:0] Data_IN,
  input  [7:0] in_2,
  input  Clock,
  input  Mem_out,
  output [15:0] out_5,
  output [15:0] out_6,
  output [15:0] Data_OUT
);

  wire delay_1_data_out, not_1_out, not_2_out, or_1_out;

  not not_1 (not_1_out, Mem_out);
  or or_1 (or_1_out, Clock, not_1_out);
  not not_2 (not_2_out, or_1_out);
  RAM #(.dataWidth(16), .databus("bidir"), .trigger("high")) ram_1 (
    .addr(in_2), .we(not_2_out), .oe(or_1_out), .data(Data_OUT));  // open: clk
  delay delay_1 (.Data_IN(Clock), .Data_OUT(delay_1_data_out));
  register_16bit register_16bit_1 (.Clock(delay_1_data_out), .Enable_low(1'b0), .Data_In(Data_IN), .Data_OUT(out_6));
  Buffer_16bit_Tristate buffer_16bit_tristate_1 (.OE(or_1_out), .Data_in(out_6), .Data_out(Data_OUT));

  assign out_5 = Data_OUT;
endmodule

module Buffer_16bit_Tristate (
  input  OE,
  input  [15:0] Data_in,
  output [15:0] Data_out
);

  _74244 #(.ShowInternalStructure("true")) u_74244_1 (
    .pin1(OE), .pin2(Data_in[0]), .pin3(Data_out[4]), .pin4(Data_in[1]), .pin5(Data_out[5]),
    .pin6(Data_in[2]), .pin7(Data_out[6]), .pin8(Data_in[3]), .pin9(Data_out[7]), .pin19(OE),
    .pin18(Data_out[0]), .pin17(Data_in[4]), .pin16(Data_out[1]), .pin15(Data_in[5]), .pin14(Data_out[2]),
    .pin13(Data_in[6]), .pin12(Data_out[3]), .pin11(Data_in[7]));
  _74244 #(.ShowInternalStructure("true")) u_74244_2 (
    .pin1(OE), .pin2(Data_in[8]), .pin3(Data_out[12]), .pin4(Data_in[9]), .pin5(Data_out[13]),
    .pin6(Data_in[10]), .pin7(Data_out[14]), .pin8(Data_in[11]), .pin9(Data_out[15]), .pin19(OE),
    .pin18(Data_out[8]), .pin17(Data_in[12]), .pin16(Data_out[9]), .pin15(Data_in[13]), .pin14(Data_out[10]),
    .pin13(Data_in[14]), .pin12(Data_out[11]), .pin11(Data_in[15]));
endmodule
