// Logisim project hack_computer.circ as structural Verilog: 11 circuits, main circuit Hack
module Hack (
  input  Clock,
  input  Reset,
  output [15:0] RAM_Data,
  output [14:0] out_4,
  output [15:0] out_5,
  output [15:0] A_Reg,
  output [15:0] D_Reg,
  output [14:0] out_8,
  output [15:0] out_9,
  output [15:0] out_10,
  output [15:0] out_11
);

  wire cpu_1_p9;

  ROM #(.addrWidth(15), .dataWidth(16)) rom_1 (.addr(out_4), .data(out_5));
  // cpu cpu_1: pin names not known; wires that end beside it: out_5, Clock, Reset, out_9, D_Reg, A_Reg, out_8, out_4, cpu_1_p9
  RAM #(.addrWidth(15), .dataWidth(16), .databus("bidir"), .enables("line")) ram_1 (
    .addr(out_8), .we(cpu_1_p9), .clk(Clock), .data(out_9));  // open: oe

  assign out_10 = A_Reg;
  assign out_11 = D_Reg;
  assign RAM_Data = out_9;

  // Notes on the sheet:
  //   contents of rom_1 (hex, n*v repeats v):
  //   8 ec10 7 e090 0 e308 6 ea87 8 a007
  //   Program Counter
  //   Instruction
  //   RAM Address
endmodule

module PC (
  input  [15:0] ADDR_IN,
  input  RESET,
  input  LOAD,
  input  INC,
  input  Clock,
  output [15:0] ADDR_OUT
);

  wire [15:0] fulladder_16_1_addout, multiplex16_1_out_pins, multiplex16_2_out_pins, multiplex16_3_out_pins;

  register_16bit register_16bit_1 (
    .Clock(Clock), .Enable_low(1'b0), .Data_In(multiplex16_3_out_pins), .Data_OUT(ADDR_OUT));
  fulladder_16 fulladder_16_1 (.B_in(ADDR_OUT), .A_in(16'h1), .AddOut(fulladder_16_1_addout));  // open: OverFlow
  multiplex16 multiplex16_1 (
    .Sel(INC), .InB(fulladder_16_1_addout), .InA(ADDR_OUT), .Out_Pins(multiplex16_1_out_pins));  // open: Strobe
  multiplex16 multiplex16_2 (
    .Sel(LOAD), .InB(ADDR_IN), .InA(multiplex16_1_out_pins), .Out_Pins(multiplex16_2_out_pins));  // open: Strobe
  multiplex16 multiplex16_3 (
    .Strobe(RESET), .InA(multiplex16_2_out_pins), .Out_Pins(multiplex16_3_out_pins));  // open: Sel, InB
endmodule

module register_16bit (
  input  Clock,
  input  Enable_low,
  input  [15:0] Data_In,
  output [15:0] Data_OUT
);

  _74377 #(.ShowInternalStructure("true")) u_74377_1 (
    .pin1(Enable_low), .pin2(Data_OUT[8]), .pin3(Data_In[8]), .pin4(Data_In[9]), .pin5(Data_OUT[9]),
    .pin6(Data_OUT[10]), .pin7(Data_In[10]), .pin8(Data_In[11]), .pin9(Data_OUT[11]), .pin19(Data_OUT[15]),
    .pin18(Data_In[15]), .pin17(Data_In[14]), .pin16(Data_OUT[14]), .pin15(Data_OUT[13]),
    .pin14(Data_In[13]), .pin13(Data_In[12]), .pin12(Data_OUT[12]), .pin11(Clock));
  _74377 #(.ShowInternalStructure("true")) u_74377_2 (
    .pin1(Enable_low), .pin2(Data_OUT[0]), .pin3(Data_In[0]), .pin4(Data_In[1]), .pin5(Data_OUT[1]),
    .pin6(Data_OUT[2]), .pin7(Data_In[2]), .pin8(Data_In[3]), .pin9(Data_OUT[3]), .pin19(Data_OUT[7]),
    .pin18(Data_In[7]), .pin17(Data_In[6]), .pin16(Data_OUT[6]), .pin15(Data_OUT[5]), .pin14(Data_In[5]),
    .pin13(Data_In[4]), .pin12(Data_OUT[4]), .pin11(Clock));
endmodule

// Adder 16
module fulladder_16 (
  input  [15:0] B_in,
  input  [15:0] A_in,
  output [15:0] AddOut,
  output OverFlow
);

  wire n74283_1_pin7, n74283_2_pin7, n74283_3_pin7;

  _74283 #(.ShowInternalStructure("true")) u_74283_1 (
    .pin1(AddOut[13]), .pin2(B_in[13]), .pin3(A_in[13]), .pin4(AddOut[12]), .pin5(A_in[12]), .pin6(B_in[12]),
    .pin7(n74283_1_pin7), .pin15(B_in[14]), .pin14(A_in[14]), .pin13(AddOut[14]), .pin12(A_in[15]),
    .pin11(B_in[15]), .pin10(AddOut[15]), .pin9(OverFlow));
  _74283 #(.ShowInternalStructure("true")) u_74283_2 (
    .pin1(AddOut[9]), .pin2(B_in[9]), .pin3(A_in[9]), .pin4(AddOut[8]), .pin5(A_in[8]), .pin6(B_in[8]),
    .pin7(n74283_2_pin7), .pin15(B_in[10]), .pin14(A_in[10]), .pin13(AddOut[10]), .pin12(A_in[11]),
    .pin11(B_in[11]), .pin10(AddOut[11]), .pin9(n74283_1_pin7));
  _74283 #(.ShowInternalStructure("true")) u_74283_3 (
    .pin1(AddOut[5]), .pin2(B_in[5]), .pin3(A_in[5]), .pin4(AddOut[4]), .pin5(A_in[4]), .pin6(B_in[4]),
    .pin7(n74283_3_pin7), .pin15(B_in[6]), .pin14(A_in[6]), .pin13(AddOut[6]), .pin12(A_in[7]),
    .pin11(B_in[7]), .pin10(AddOut[7]), .pin9(n74283_2_pin7));
  _74283 #(.ShowInternalStructure("true")) u_74283_4 (
    .pin1(AddOut[1]), .pin2(B_in[1]), .pin3(A_in[1]), .pin4(AddOut[0]), .pin5(A_in[0]), .pin6(B_in[0]),
    .pin15(B_in[2]), .pin14(A_in[2]), .pin13(AddOut[2]), .pin12(A_in[3]), .pin11(B_in[3]), .pin10(AddOut[3]),
    .pin9(n74283_3_pin7));  // open: pin7
endmodule

module multiplex16 (
  input  Strobe,
  input  Sel,
  input  [15:0] InB,
  input  [15:0] InA,
  output [15:0] Out_Pins
);

  _74157 #(.ShowInternalStructure("true")) u_74157_1 (
    .pin1(Sel), .pin2(InA[15]), .pin3(InB[15]), .pin4(Out_Pins[15]), .pin5(InA[14]), .pin6(InB[14]),
    .pin7(Out_Pins[14]), .pin15(Strobe), .pin14(InA[12]), .pin13(InB[12]), .pin12(Out_Pins[12]),
    .pin11(InA[13]), .pin10(InB[13]), .pin9(Out_Pins[13]));
  _74157 #(.ShowInternalStructure("true")) u_74157_2 (
    .pin1(Sel), .pin2(InA[11]), .pin3(InB[11]), .pin4(Out_Pins[11]), .pin5(InA[10]), .pin6(InB[10]),
    .pin7(Out_Pins[10]), .pin15(Strobe), .pin14(InA[8]), .pin13(InB[8]), .pin12(Out_Pins[8]), .pin11(InA[9]),
    .pin10(InB[9]), .pin9(Out_Pins[9]));
  _74157 #(.ShowInternalStructure("true")) u_74157_3 (
    .pin1(Sel), .pin2(InA[7]), .pin3(InB[7]), .pin4(Out_Pins[7]), .pin5(InA[6]), .pin6(InB[6]),
    .pin7(Out_Pins[6]), .pin15(Strobe), .pin14(InA[4]), .pin13(InB[4]), .pin12(Out_Pins[4]), .pin11(InA[5]),
    .pin10(InB[5]), .pin9(Out_Pins[5]));
  _74157 #(.ShowInternalStructure("true")) u_74157_4 (
    .pin1(Sel), .pin2(InA[3]), .pin3(InB[3]), .pin4(Out_Pins[3]), .pin5(InA[2]), .pin6(InB[2]),
    .pin7(Out_Pins[2]), .pin15(Strobe), .pin14(InA[0]), .pin13(InB[0]), .pin12(Out_Pins[0]), .pin11(InA[1]),
    .pin10(InB[1]), .pin9(Out_Pins[1]));
endmodule

module ALU (
  input  no,
  input  f,
  input  nx,
  input  zx,
  input  [15:0] x,
  input  ny,
  input  zy,
  input  [15:0] y,
  output [15:0] ALU_out,
  output zr,
  output ng
);

  wire or_8bit_1_out_nor, or_8bit_2_out_nor;
  wire [15:0] and16_16_1_out_pins, fulladder_16_1_addout, multiplex16_1_out_pins, multiplex16_2_out_pins,
       multiplex16_3_out_pins, multiplex16_xor_1_out_pins, multiplex16_xor_2_out_pins;

  multiplex16 multiplex16_1 (.Strobe(zx), .InA(x), .Out_Pins(multiplex16_1_out_pins));  // open: Sel, InB
  multiplex16 multiplex16_2 (.Strobe(zy), .InA(y), .Out_Pins(multiplex16_2_out_pins));  // open: Sel, InB
  OR_8bit or_8bit_1 (.In_OR(ALU_out[7:0]), .Out_NOR(or_8bit_1_out_nor));  // open: Out_OR
  OR_8bit or_8bit_2 (.In_OR(ALU_out[15:8]), .Out_NOR(or_8bit_2_out_nor));  // open: Out_OR
  Multiplex16_XOR multiplex16_xor_1 (
    .Invert(nx), .IN_Pins(multiplex16_1_out_pins), .OUT_Pins(multiplex16_xor_1_out_pins));
  Multiplex16_XOR multiplex16_xor_2 (
    .Invert(ny), .IN_Pins(multiplex16_2_out_pins), .OUT_Pins(multiplex16_xor_2_out_pins));
  _7408 #(.ShowInternalStructure("true")) u_7408_1 (
    .pin10(or_8bit_2_out_nor), .pin9(or_8bit_1_out_nor), .pin8(zr));  // open: pin1, pin2, pin3, pin4, pin5, pin6, pin13, pin12, pin11
  fulladder_16 fulladder_16_1 (
    .B_in(multiplex16_xor_1_out_pins), .A_in(multiplex16_xor_2_out_pins), .AddOut(fulladder_16_1_addout));  // open: OverFlow
  and16_16 and16_16_1 (
    .InB(multiplex16_xor_1_out_pins), .InA(multiplex16_xor_2_out_pins), .Out_Pins(and16_16_1_out_pins));
  multiplex16 multiplex16_3 (
    .Sel(f), .InB(fulladder_16_1_addout), .InA(and16_16_1_out_pins), .Out_Pins(multiplex16_3_out_pins));  // open: Strobe
  Multiplex16_XOR multiplex16_xor_3 (.Invert(no), .IN_Pins(multiplex16_3_out_pins), .OUT_Pins(ALU_out));

  assign ng = ALU_out[15];
endmodule

module Multiplex16_XOR (
  input  Invert,
  input  [15:0] IN_Pins,
  output [15:0] OUT_Pins
);

  _7486 #(.ShowInternalStructure("true")) u_7486_1 (
    .pin1(Invert), .pin2(IN_Pins[13]), .pin3(OUT_Pins[13]), .pin4(Invert), .pin5(IN_Pins[12]),
    .pin6(OUT_Pins[12]), .pin13(Invert), .pin12(IN_Pins[14]), .pin11(OUT_Pins[14]), .pin10(Invert),
    .pin9(IN_Pins[15]), .pin8(OUT_Pins[15]));
  _7486 #(.ShowInternalStructure("true")) u_7486_2 (
    .pin1(Invert), .pin2(IN_Pins[9]), .pin3(OUT_Pins[9]), .pin4(Invert), .pin5(IN_Pins[8]),
    .pin6(OUT_Pins[8]), .pin13(Invert), .pin12(IN_Pins[10]), .pin11(OUT_Pins[10]), .pin10(Invert),
    .pin9(IN_Pins[11]), .pin8(OUT_Pins[11]));
  _7486 #(.ShowInternalStructure("true")) u_7486_3 (
    .pin1(Invert), .pin2(IN_Pins[5]), .pin3(OUT_Pins[5]), .pin4(Invert), .pin5(IN_Pins[4]),
    .pin6(OUT_Pins[4]), .pin13(Invert), .pin12(IN_Pins[6]), .pin11(OUT_Pins[6]), .pin10(Invert),
    .pin9(IN_Pins[7]), .pin8(OUT_Pins[7]));
  _7486 #(.ShowInternalStructure("true")) u_7486_4 (
    .pin1(Invert), .pin2(IN_Pins[1]), .pin3(OUT_Pins[1]), .pin4(Invert), .pin5(IN_Pins[0]),
    .pin6(OUT_Pins[0]), .pin13(Invert), .pin12(IN_Pins[2]), .pin11(OUT_Pins[2]), .pin10(Invert),
    .pin9(IN_Pins[3]), .pin8(OUT_Pins[3]));
endmodule

module and16_16 (
  input  [15:0] InB,
  input  [15:0] InA,
  output [15:0] Out_Pins
);

  _7408 #(.ShowInternalStructure("true")) u_7408_1 (
    .pin1(InA[15]), .pin2(InB[15]), .pin3(Out_Pins[15]), .pin4(InA[14]), .pin5(InB[14]), .pin6(Out_Pins[14]),
    .pin13(InA[12]), .pin12(InB[12]), .pin11(Out_Pins[12]), .pin10(InA[13]), .pin9(InB[13]),
    .pin8(Out_Pins[13]));
  _7408 #(.ShowInternalStructure("true")) u_7408_2 (
    .pin1(InA[11]), .pin2(InB[11]), .pin3(Out_Pins[11]), .pin4(InA[10]), .pin5(InB[10]), .pin6(Out_Pins[10]),
    .pin13(InA[8]), .pin12(InB[8]), .pin11(Out_Pins[8]), .pin10(InA[9]), .pin9(InB[9]), .pin8(Out_Pins[9]));
  _7408 #(.ShowInternalStructure("true")) u_7408_3 (
    .pin1(InA[7]), .pin2(InB[7]), .pin3(Out_Pins[7]), .pin4(InA[6]), .pin5(InB[6]), .pin6(Out_Pins[6]),
    .pin13(InA[4]), .pin12(InB[4]), .pin11(Out_Pins[4]), .pin10(InA[5]), .pin9(InB[5]), .pin8(Out_Pins[5]));
  _7408 #(.ShowInternalStructure("true")) u_7408_4 (
    .pin1(InA[3]), .pin2(InB[3]), .pin3(Out_Pins[3]), .pin4(InA[2]), .pin5(InB[2]), .pin6(Out_Pins[2]),
    .pin13(InA[0]), .pin12(InB[0]), .pin11(Out_Pins[0]), .pin10(InA[1]), .pin9(InB[1]), .pin8(Out_Pins[1]));
endmodule

module cpu (
  input  [15:0] Instruction,
  input  [15:0] inM,
  input  M_M,
  input  Reset,
  input  Clock,
  output [15:0] OutM,
  output [15:0] Debug_D,
  output [15:0] Debug_A,
  output [14:0] AddressM,
  output [14:0] AddressInstr,
  output writeM
);

  wire and_1_out, and_2_out, button_1_out, counter_744017_1_q0, counter_744017_1_q1, counter_744017_1_q2,
       counter_744017_1_q3, counter_744017_2_q0, counter_744017_2_q1, counter_744017_2_q2,
       counter_744017_2_q3, n7404_1_pin2, n7404_1_pin4, n7404_1_pin5, n7404_1_pin6, n7404_1_pin10,
       n7404_1_pin12, n7404_1_pin13, n7408_1_pin1, n7408_1_pin3, n7408_1_pin6, n7408_1_pin11, n7408_1_pin13,
       n7408_2_pin3, n7432_1_pin1, n7432_1_pin2, n7432_1_pin3, n7432_1_pin5, n7432_1_pin6, n7432_1_pin10,
       n7432_1_pin12, n74244_1_pin1, not_1_out, or_1_out;
  wire [15:0] alu_1_alu_out, multiplex16_1_out_pins;
  wire [15:15] pc_1_addr_out, register_16bit_1_data_out;

  _7408 #(.ShowInternalStructure("true")) u_7408_1 (
    .pin1(n7408_1_pin1), .pin2(Instruction[1]), .pin3(n7408_1_pin3), .pin4(Instruction[15]),
    .pin5(Instruction[4]), .pin6(n7408_1_pin6), .pin13(n7408_1_pin13), .pin12(Instruction[15]),
    .pin11(n7408_1_pin11), .pin10(Instruction[3]), .pin9(Instruction[15]));  // open: pin8
  counter_744017 counter_744017_1 (
    .CP0(Clock), .MR(n7432_1_pin6), .Q0(counter_744017_1_q0), .Q1(counter_744017_1_q1),
    .Q2(counter_744017_1_q2), .Q3(counter_744017_1_q3));  // open: nCP1, Q4, Q5, Q6, Q7, Q8, Q9, nQ5_9
  multiplex16 multiplex16_1 (
    .Sel(Instruction[15]), .InB(alu_1_alu_out), .InA(Instruction), .Out_Pins(multiplex16_1_out_pins));  // open: Strobe
  _7404 #(.ShowInternalStructure("true")) u_7404_1 (
    .pin1(Reset), .pin2(n7404_1_pin2), .pin3(Instruction[9]), .pin4(n7404_1_pin4), .pin5(n7404_1_pin5),
    .pin6(n7404_1_pin6), .pin13(n7404_1_pin13), .pin12(n7404_1_pin12), .pin11(n7408_1_pin6),
    .pin10(n7404_1_pin10), .pin9(Instruction[5]), .pin8(n7408_1_pin13));
  register_16bit register_16bit_1 (
    .Clock(counter_744017_1_q1), .Enable_low(n7408_1_pin11), .Data_In(multiplex16_1_out_pins),
    .Data_OUT({register_16bit_1_data_out[15], AddressM}));
  _7432 #(.ShowInternalStructure("true")) u_7432_1 (
    .pin1(n7432_1_pin1), .pin2(n7432_1_pin2), .pin3(n7432_1_pin3), .pin4(counter_744017_1_q3),
    .pin5(n7432_1_pin5), .pin6(n7432_1_pin6), .pin13(n7408_1_pin3), .pin12(n7432_1_pin12),
    .pin11(n7432_1_pin1), .pin10(n7432_1_pin10), .pin9(n7408_1_pin1), .pin8(n7404_1_pin5));
  _7408 #(.ShowInternalStructure("true")) u_7408_2 (
    .pin1(n7432_1_pin3), .pin2(Instruction[15]), .pin3(n7408_2_pin3), .pin4(n7404_1_pin13),
    .pin5(counter_744017_1_q2), .pin6(writeM), .pin13(n7404_1_pin6), .pin12(Instruction[0]),
    .pin11(n7432_1_pin2), .pin10(Instruction[2]), .pin9(n7432_1_pin10), .pin8(n7432_1_pin12));
  multiplex16 multiplex16_2 (
    .Sel(Instruction[12]), .InB(inM), .InA({register_16bit_1_data_out[15], AddressM}), .Out_Pins(Debug_A));  // open: Strobe
  _7421 #(.ShowInternalStructure("true")) u_7421_1 (
    .pin1(n7404_1_pin12), .pin2(n7404_1_pin12), .pin4(counter_744017_1_q2), .pin5(counter_744017_1_q2),
    .pin6(n7432_1_pin5), .pin13(Instruction[15]), .pin12(Instruction[12]), .pin10(Instruction[3]),
    .pin9(n7404_1_pin4), .pin8(n7404_1_pin13));  // open: pin3, pin11
  ALU alu_1 (
    .no(Instruction[6]), .f(Instruction[7]), .nx(Instruction[10]), .zx(Instruction[11]), .x(Debug_D),
    .ny(Instruction[8]), .zy(Instruction[9]), .y(Debug_A), .ALU_out(alu_1_alu_out), .zr(n7408_1_pin1),
    .ng(n7432_1_pin10));
  Button button_1 (.out(button_1_out));
  PC pc_1 (
    .ADDR_IN({register_16bit_1_data_out[15], AddressM}), .RESET(Reset), .LOAD(n7408_2_pin3),
    .INC(n7404_1_pin2), .Clock(counter_744017_1_q0), .ADDR_OUT({pc_1_addr_out[15], AddressInstr}));
  register_16bit register_16bit_2 (
    .Clock(counter_744017_1_q1), .Enable_low(n7404_1_pin10), .Data_In(alu_1_alu_out), .Data_OUT(Debug_D));
  counter_744017 counter_744017_2 (
    .CP0(button_1_out), .MR(or_1_out), .Q0(counter_744017_2_q0), .Q1(counter_744017_2_q1),
    .Q2(counter_744017_2_q2), .Q3(counter_744017_2_q3));  // open: nCP1, Q4, Q5, Q6, Q7, Q8, Q9, nQ5_9
  or or_1 (or_1_out, counter_744017_2_q3, and_1_out);
  and and_1 (and_1_out, counter_744017_2_q2, not_1_out);
  _74244 #(.ShowInternalStructure("true")) u_74244_1 (
    .pin1(n74244_1_pin1), .pin2(alu_1_alu_out[4]), .pin3(OutM[3]), .pin4(alu_1_alu_out[5]), .pin5(OutM[2]),
    .pin6(alu_1_alu_out[6]), .pin7(OutM[1]), .pin8(alu_1_alu_out[7]), .pin9(OutM[0]), .pin19(n74244_1_pin1),
    .pin18(OutM[4]), .pin17(alu_1_alu_out[3]), .pin16(OutM[5]), .pin15(alu_1_alu_out[2]), .pin14(OutM[6]),
    .pin13(alu_1_alu_out[1]), .pin12(OutM[7]), .pin11(alu_1_alu_out[0]));
  _74244 #(.ShowInternalStructure("true")) u_74244_2 (
    .pin1(n74244_1_pin1), .pin2(alu_1_alu_out[12]), .pin3(OutM[11]), .pin4(alu_1_alu_out[13]),
    .pin5(OutM[10]), .pin6(alu_1_alu_out[14]), .pin7(OutM[9]), .pin8(alu_1_alu_out[15]), .pin9(OutM[8]),
    .pin19(n74244_1_pin1), .pin18(OutM[12]), .pin17(alu_1_alu_out[11]), .pin16(OutM[13]),
    .pin15(alu_1_alu_out[10]), .pin14(OutM[14]), .pin13(alu_1_alu_out[9]), .pin12(OutM[15]),
    .pin11(alu_1_alu_out[8]));
  not not_1 (not_1_out, M_M);
  LED led_1 (.in(counter_744017_2_q0));
  LED led_2 (.in(counter_744017_2_q1));
  and and_2 (and_2_out, M_M, counter_744017_2_q2);
  LED led_3 (.in(and_2_out));
endmodule

module OR_8bit (
  input  [7:0] In_OR,
  output Out_NOR,
  output Out_OR
);

  or or_1 (Out_OR, In_OR[0], In_OR[1], In_OR[2], In_OR[3], In_OR[4], In_OR[5], In_OR[6], In_OR[7]);
  not not_1 (Out_NOR, Out_OR);
endmodule

module counter_744017 (
  input  nCP1,
  input  CP0,
  input  MR,
  output Q0,
  output Q1,
  output Q2,
  output Q3,
  output Q4,
  output Q5,
  output Q6,
  output Q7,
  output Q8,
  output Q9,
  output nQ5_9
);

  wire and_1_out, and_2_out, buffer_1_out, buffer_2_out, d_ff_1_q, d_ff_1_qn, d_ff_2_q, d_ff_2_qn, d_ff_3_q,
       d_ff_3_qn, d_ff_4_q, d_ff_4_qn, d_ff_5_q, d_ff_5_qn, nor_1_out, nor_2_out, nor_3_out, nor_4_out,
       nor_5_out, nor_6_out, nor_7_out, nor_8_out, nor_9_out, nor_10_out, not_1_out, or_1_out;

  not not_1 (not_1_out, nCP1);
  buf buffer_1 (buffer_1_out, CP0);
  buf buffer_2 (buffer_2_out, MR);
  nor nor_1 (nor_1_out, d_ff_5_q, d_ff_1_q);
  buf buffer_3 (Q0, nor_1_out);
  D_Flip_Flop d_ff_1 (
    .D(d_ff_5_qn), .clk(and_1_out), .Q(d_ff_1_q), .Qn(d_ff_1_qn), .reset(buffer_2_out));  // open: preset
  and and_1 (and_1_out, not_1_out, buffer_1_out);
  nor nor_2 (nor_2_out, d_ff_2_q, d_ff_1_qn);
  nor nor_3 (nor_3_out, d_ff_2_qn, d_ff_3_q);
  buf buffer_4 (Q1, nor_2_out);
  buf buffer_5 (Q2, nor_3_out);
  nor nor_4 (nor_4_out, d_ff_4_q, d_ff_3_qn);
  nor nor_5 (nor_5_out, d_ff_5_q, d_ff_4_qn);
  buf buffer_6 (Q3, nor_4_out);
  buf buffer_7 (Q4, nor_5_out);
  or or_1 (or_1_out, d_ff_3_q, d_ff_1_q);
  D_Flip_Flop d_ff_2 (
    .D(d_ff_1_q), .clk(and_1_out), .Q(d_ff_2_q), .Qn(d_ff_2_qn), .reset(buffer_2_out));  // open: preset
  nor nor_6 (nor_6_out, d_ff_1_qn, d_ff_5_qn);
  nor nor_7 (nor_7_out, d_ff_1_q, d_ff_2_qn);
  buf buffer_8 (Q5, nor_6_out);
  buf buffer_9 (Q6, nor_7_out);
  and and_2 (and_2_out, or_1_out, d_ff_2_q);
  D_Flip_Flop d_ff_3 (
    .D(and_2_out), .clk(and_1_out), .Q(d_ff_3_q), .Qn(d_ff_3_qn), .reset(buffer_2_out));  // open: preset
  nor nor_8 (nor_8_out, d_ff_2_q, d_ff_3_qn);
  nor nor_9 (nor_9_out, d_ff_4_qn, d_ff_3_q);
  buf buffer_10 (Q7, nor_8_out);
  buf buffer_11 (Q8, nor_9_out);
  D_Flip_Flop d_ff_4 (
    .D(d_ff_3_q), .clk(and_1_out), .Q(d_ff_4_q), .Qn(d_ff_4_qn), .reset(buffer_2_out));  // open: preset
  nor nor_10 (nor_10_out, d_ff_4_q, d_ff_5_qn);
  buf buffer_12 (Q9, nor_10_out);
  buf buffer_13 (nQ5_9, d_ff_5_qn);
  D_Flip_Flop d_ff_5 (
    .D(d_ff_4_q), .clk(and_1_out), .Q(d_ff_5_q), .Qn(d_ff_5_qn), .reset(buffer_2_out));  // open: preset
endmodule
